// Logisim project Nunes_Vaca 1.circ as structural Verilog: 6 circuits, main circuit animaux_top
module animaux_top (
  input  quatre_pattes,
  input  ecailles,
  input  ovipare,
  input  ovovivipare,
  output ours,
  output oiseau,
  output ornithorynque,
  output lezard,
  output serpent,
  output animal_indetermine
);

  ours_man ours_man_1 (
    .quatre_pattes(quatre_pattes), .ecailles(ecailles), .ovipare(ovipare), .ovovivipare(ovovivipare),
    .ours(ours));
  oiseau_man oiseau_man_1 (
    .quatre_pattes(quatre_pattes), .ecailles(ecailles), .ovipare(ovipare), .ovovivipare(ovovivipare),
    .oiseau(oiseau));
  ornithorynque_auto ornithorynque_auto_1 (
    .quatre_pattes(quatre_pattes), .ecailles(ecailles), .ovipare(ovipare), .ovovivipare(ovovivipare),
    .ornithorynque(ornithorynque));
  lezard_man lezard_man_1 (
    .quatre_pattes(quatre_pattes), .ecailles(ecailles), .ovipare(ovipare), .ovovivipare(ovovivipare),
    .lezard(lezard));
  serpent_auto serpent_auto_1 (
    .quatre_pattes(quatre_pattes), .ecailles(ecailles), .ovipare(ovipare), .ovovivipare(ovovivipare),
    .serpent(serpent));
  nor nor_1 (animal_indetermine, ours, oiseau, ornithorynque, lezard, serpent);
endmodule

module ours_man (
  input  quatre_pattes,
  input  ecailles,
  input  ovipare,
  input  ovovivipare,
  output ours
);

  wire not_1_out, not_2_out, not_3_out;

  not not_1 (not_1_out, ecailles);
  not not_2 (not_2_out, ovipare);
  not not_3 (not_3_out, ovovivipare);
  and and_1 (ours, quatre_pattes, not_1_out, not_2_out, not_3_out);
endmodule

module oiseau_man (
  input  quatre_pattes,
  input  ecailles,
  input  ovipare,
  input  ovovivipare,
  output oiseau
);

  wire not_1_out, not_2_out, not_3_out;

  not not_1 (not_1_out, quatre_pattes);
  not not_2 (not_2_out, ecailles);
  not not_3 (not_3_out, ovovivipare);
  and and_1 (oiseau, not_1_out, not_2_out, ovipare, not_3_out);
endmodule

module lezard_man (
  input  quatre_pattes,
  input  ecailles,
  input  ovipare,
  input  ovovivipare,
  output lezard
);

  wire or_1_out;

  or or_1 (or_1_out, ovipare, ovovivipare);
  and and_1 (lezard, quatre_pattes, ecailles, or_1_out);
endmodule

module ornithorynque_auto (
  input  quatre_pattes,
  input  ecailles,
  input  ovipare,
  input  ovovivipare,
  output ornithorynque
);

  wire not_1_out, not_2_out;

  not not_1 (not_1_out, ecailles);
  not not_2 (not_2_out, ovipare);
  and and_1 (ornithorynque, quatre_pattes, not_1_out, not_2_out, ovovivipare);
endmodule

module serpent_auto (
  input  quatre_pattes,
  input  ecailles,
  input  ovipare,
  input  ovovivipare,
  output serpent
);

  wire not_1_out, or_1_out;

  not not_1 (not_1_out, quatre_pattes);
  or or_1 (or_1_out, ovipare, ovovivipare);
  and and_1 (serpent, not_1_out, ecailles, or_1_out);
endmodule
