// Logisim project nunes_vaca.circ as structural Verilog: 3 circuits, main circuit bin_lin_3a8_top
module bin_lin_3a8_top (
);

  wire dipswitch_1_sw1, dipswitch_1_sw2;
  wire [2:0] dipswitch_1_sw6;
  wire [7:0] bin_lin_3a8_1_lin_o;

  DipSwitch dipswitch_1 (
    .sw1(dipswitch_1_sw1), .sw2(dipswitch_1_sw2), .sw6(dipswitch_1_sw6[0]), .sw7(dipswitch_1_sw6[1]),
    .sw8(dipswitch_1_sw6[2]));  // open: sw3, sw4, sw5
  bin_lin_3a8 bin_lin_3a8_1 (
    .en_i(dipswitch_1_sw1), .sel_i(dipswitch_1_sw2), .bin_i(dipswitch_1_sw6), .lin_o(bin_lin_3a8_1_lin_o));
  // NoConnect on nothing
  // PortIO #(.number(25)) portio_1: pin names not known; wires that end beside it: 1'b1, {{17{1'b0}}, bin_lin_3a8_1_lin_o}
endmodule

module bin_lin_3a8_sim (
  input  En,
  input  Sel,
  input  [2:0] Bin
);

  wire [7:0] bin_lin_3a8_1_lin_o;

  LED Lin7 (.in(bin_lin_3a8_1_lin_o[7]));
  LED Lin6 (.in(bin_lin_3a8_1_lin_o[6]));
  LED Lin5 (.in(bin_lin_3a8_1_lin_o[5]));
  LED Lin4 (.in(bin_lin_3a8_1_lin_o[4]));
  bin_lin_3a8 bin_lin_3a8_1 (.en_i(En), .sel_i(Sel), .bin_i(Bin), .lin_o(bin_lin_3a8_1_lin_o));
  LED Lin3 (.in(bin_lin_3a8_1_lin_o[3]));
  LED Lin2 (.in(bin_lin_3a8_1_lin_o[2]));
  LED Lin1 (.in(bin_lin_3a8_1_lin_o[1]));
  LED Lin0 (.in(bin_lin_3a8_1_lin_o[0]));
endmodule

module bin_lin_3a8 (
  input  en_i,
  input  sel_i,
  input  [2:0] bin_i,
  output [7:0] lin_o
);

  wire or_1_out;

  or or_1 (or_1_out, en_i, sel_i);
  // AND_Gate and_1 has open pins: in0=or_1_out, in1=sel_i, out=open

  // Notes on the sheet:
  //   Ne pas modifier les entrées sorties !
endmodule
